// Logisim project ALU.circ as structural Verilog: 1 circuit, main circuit main
module main (
  input  [2:0] oper,
  input  enable,
  input  [7:0] in0,
  input  [7:0] out0,
  input  [7:0] in1
);

  wire add, No_op;
  wire [7:0] controlled_buffer_1_out, controlled_buffer_2_out;

  Decoder #(.select(3)) decoder_1 (
    .out0(No_op), .out1(add), .sel(oper), .en(enable));  // open: out2, out3, out4, out5, out6, out7
  Controlled_Buffer #(.width(8)) controlled_buffer_1 (.in(in0), .out(controlled_buffer_1_out));  // open: en
  Controlled_Buffer #(.width(8)) controlled_buffer_2 (.in(in1), .out(controlled_buffer_2_out));  // open: en
  Adder adder_1 (.a(controlled_buffer_1_out), .b(controlled_buffer_2_out), .out(out0));  // open: cin, cout

  // Notes on the sheet:
  //   Decoder
endmodule
